# Fritzing sketch sensor de corrente (saved by Fritzing 0.9.3b)
circuit board: 8.46667cm x 5.64444cm
breadboards: 1

parts:
  R1 = Resistor [tolerance=±5% resistance=12k package=THT]
  R2 = Resistor [tolerance=±5% resistance=12k package=THT]
  C1 = Electrolytic Capacitor [capacitance=10µF voltage=16V package="100 mil [THT, electrolytic]"]
  R3 = Resistor [tolerance=±5% resistance=33 package=THT]
  U2 = NodeMCU V3.0 [part_number="Lolin v0.1"]
  MIC1 = Microphone
  R4 = Resistor [tolerance=±5% resistance=260 package=THT]
  R5 = Resistor [tolerance=±5% resistance=260 package=THT]

nets:
  N1: R1.Pin_0, U2.3V3
  N2: R1.Pin_1, R2.Pin_0, C1.+, R3.Pin_0, R3.Pin_1, MIC1.pin1, MIC1.pin2, R4.Pin_0
  N3: R2.Pin_1, C1.-, U2.GND#13, U2.GND#16, U2.GND#33
  N4: U2.A0, R4.Pin_1, R5.Pin_0
  GND: R5.Pin_1

custom parts:
  NodeMCU V3.0: ESP8266 based NodeMCU
